# Fritzing sketch Makerspace_IoT_Schematic_Fritzing (saved by Fritzing 0.9.3b)
breadboards: 1

parts:
  Teensy_3_1 = Teensy 3.0
  Teensy = InvenSense MPU6050

nets:
  GND: Teensy_3_1.GND, Teensy.GND
  N1: Teensy_3_1.A4/D18, Teensy.SDA
  N2: Teensy_3_1.A5/D19, Teensy.SCL
  VIN: Teensy_3_1.Vin, Teensy.VCC
