# Fritzing sketch V2_Makerspace_IoT_Schematic_Fritzing (saved by Fritzing 0.9.3b)
breadboards: 1

parts:
  Part1 = InvenSense MPU6050
  Teensy_LC1 = Teensy-LC
  MLX906 = gy-906

nets:
  VCC: Part1.VCC, Teensy_LC1.3V3, MLX906.VIN
  GND: Part1.GND, Teensy_LC1.GND, MLX906.GND
  N1: Part1.SCL, Teensy_LC1.A5/D19, MLX906.SCL
  N2: Part1.SDA, Teensy_LC1.A6/D20, MLX906.SDA

custom parts:
  Teensy-LC: Teensy-LC (Low Cost) is a powerful 32 bit microcontroller board, with a rich set of hardware peripherals, at a very affordable price! Teensy-LC delivers an impressive collection of capabilities to make modern electronic projects simpler. It features an ARM Cortex-M0+ processor at 48 MHz, 62K Flash, 8K RAM, 12 bit analog input & output, hardware Serial, SPI & I2C, USB, and a total of 27 I/O pins.
  gy-906: gy-906 Non-contact PIR I2C interface temperature sensor breakout board.
