# Fritzing sketch ACSN250 circuit diagram (saved by Fritzing 0.9.3b)
breadboards: 1

parts:
  U1 = RELAY [package=relay-g5q]
  U2 = RELAY [package=relay-g5q]
  Teensy_3_2 = Teensy 3.1

nets:
  5V: U1.MAIN
  N1: U1.NO, U2.COIL1
  GND: U2.COIL2
  N2: U2.MAIN, Teensy_3_2.D0
  N3: U2.NO, Teensy_3_2.GND

notes:
  ACSN250
